// Logisim project cirkut z notem i 2 andami.circ as structural Verilog: 1 circuit, main circuit main
module main (
  input  in_1,
  output out_2
);

  wire and_1_out, clock_1_out, j_k_ff_1_q, j_k_ff_2_q, j_k_ff_2_qn, not_1_out;

  Clock clock_1 (.out(clock_1_out));
  and and_1 (and_1_out, j_k_ff_1_q, in_1);
  not not_1 (not_1_out, in_1);
  J_K_Flip_Flop j_k_ff_1 (.J(in_1), .clk(clock_1_out), .K(j_k_ff_2_qn), .Q(j_k_ff_1_q));  // open: Qn, preset, en, reset
  J_K_Flip_Flop j_k_ff_2 (
    .J(and_1_out), .clk(clock_1_out), .K(not_1_out), .Q(j_k_ff_2_q), .Qn(j_k_ff_2_qn));  // open: preset, en, reset
  and and_2 (out_2, j_k_ff_1_q, j_k_ff_2_q);
endmodule
